# Fritzing sketch 1W_4_LED_CIRCUIT (saved by Fritzing 0.9.2b)
breadboards: 1

parts:
  Part1 = Arduino Uno (Rev3)
  Part3 = Breadboard Power Supply Board SMD
  R1 = Resistor [tolerance=±5% resistance=220 package=THT]
  FET2 = STP16NF06 N-Channel Power MOSFET
  LED1 = LEDs [package=led10mm]
  R2 = Resistor [tolerance=±5% resistance=220 package=THT]
  R3 = Resistor [tolerance=±5% resistance=220 package=THT]
  R4 = Resistor [tolerance=±5% resistance=220 package=THT]
  FET3 = STP16NF06 N-Channel Power MOSFET
  FET5 = STP16NF06 N-Channel Power MOSFET
  LED2 = LEDs [package=led10mm]
  LED3 = LEDs [package=led10mm]
  LED4 = LEDs [package=led10mm]  # not connected
  FET6 = STP16NF06 N-Channel Power MOSFET  # not connected

nets:
  N1: Part1.D8, R1.Pin_0
  N2: Part1.D9_PWM, R2.Pin_0
  N3: Part1.D10_PWM/SS, R3.Pin_0
  N4: Part1.D11_PWM/MOSI, R4.Pin_0
  VIN: Part1.VIN, Part3.VIN
  N5: R1.Pin_1, FET2.gate
  N6: FET2.drain, LED1.A
  N7: FET3.drain, LED3.A
  N8: FET5.drain, LED2.A

notes:
  GND
  3.3.V power supply
  3.3.V

custom parts:
  STP16NF06 N-Channel Power MOSFET: STP16NF06 N-channel Power MOSFET
