# Fritzing sketch 1W_LED (saved by Fritzing 0.9.2b)
breadboards: 1

parts:
  Part1 = Arduino Uno (Rev3)
  R1 = Resistor [tolerance=±5% resistance=220 package=THT]
  Q1 = TIP120 Hi-Current Darlington Transistor

nets:
  N1: Part1.D8, R1.Pin_0
  N2: Part1.GND, Q1.EMITTER
  N3: R1.Pin_1, Q1.BASE

notes:
  1W White LED
  External Power Supply - 3.3.V
